// Logisim project Lab 4 Given.circ as structural Verilog: 14 circuits, main circuit Main
module Main (
);

  wire alu_1_zero, ALUSrc, and_1_out, Branch, Clock, comparator_1_eq, MemRead, MemtoReg, MemWrite,
       Passed_Branch, Passed_MemRead, Passed_MemtoReg, Passed_MemWrite, Passed_RegWrite, PCSrc, RegDst,
       RegWrite, Saved_ALUSrc, Saved_Branch, Saved_MemRead, Saved_MemtoReg, Saved_MemWrite, Saved_RegDst,
       Saved_RegWrite, Saved_Zero_Value, Stored_MemtoReg, Stored_RegWrite;
  wire [1:0] ALUOp, ForwardA, ForwardB, Saved_ALUOp;
  wire [3:0] ALUCtl;
  wire [4:0] Destination_Register, multiplexer_6_out, Passed_Chosen_Register, Saved_Chosen_Register,
       Saved_Destination_Register, Saved_Shmt, Saved_Source_Register, Saved_Target_Register, Shmt,
       Source_Register, Target_Register;
  wire [5:0] Funct, Opcode, Saved_Funct;
  wire [31:0] adder_2_out, alu_1_aluresult, bit_extender_1_out, Chosen_Write_Data, Current_Instruction,
       multiplexer_1_out, multiplexer_2_out, multiplexer_3_out, multiplexer_4_out, multiplexer_5_out,
       Passed_ALU_Result, Passed_Next_Instruction, Passed_Read_data_2, PC__4, ram_1_data,
       register_file_1_rddata1, register_file_1_rddata2, Saved_Adder_Result, Saved_ALU_Result,
       Saved_Mem_Data, Saved_Next_Instruction, Saved_Read_data_1, Saved_Read_data_2,
       Saved_Sign_Extended_Instruction, shifter_1_out, Stored_PC;

  // Probe on PC__4
  // Probe on Saved_Adder_Result
  Clock u_Clock (.out(Clock));
  Multiplexer #(.width(32), .enable("false")) multiplexer_1 (
    .in0(PC__4), .in1(Saved_Adder_Result), .out(multiplexer_1_out), .sel(PCSrc));
  // Probe on Stored_PC
  Register #(.width(32)) PC (.D(multiplexer_1_out), .Q(Stored_PC), .clk(Clock));  // open: en, clr
  ROM #(.dataWidth(32)) rom_1 (.addr(Stored_PC[9:2]), .data(Current_Instruction));  // open: sel
  Adder #(.width(32)) adder_1 (.a(Stored_PC), .b(32'h4), .out(PC__4));  // open: cin, cout
  // Probe on Current_Instruction
  // Probe on PC__4
  IF_ID if_id_1 (
    .Current_Instruction(Current_Instruction), .Clock(Clock),
    .Current_Instruction_2({Opcode, Source_Register, Target_Register, Destination_Register, Shmt, Funct}),
    .Next_Instruction(PC__4), .Saved_Next_Instruction(Saved_Next_Instruction));
  // Probe on Saved_Next_Instruction
  // Probe on {Opcode, Source_Register, Target_Register, Destination_Register, Shmt, Funct}
  // Probe on Funct
  // Probe on Shmt
  // Probe on Destination_Register
  // Probe on Target_Register
  // Probe on Source_Register
  // Probe on Opcode
  Main_Control main_control_1 (
    .Opcode(Opcode), .Funct(Funct), .Branch(Branch), .ALUSrc(ALUSrc), .ALUOp(ALUOp), .RegDst(RegDst),
    .MemWrite(MemWrite), .MemRead(MemRead), .MemtoReg(MemtoReg), .RegWrite(RegWrite));
  // Probe on Passed_Chosen_Register
  // Probe on Chosen_Write_Data
  // Probe on Source_Register
  // Probe on Target_Register
  Register_File register_file_1 (
    .WrAddr(Passed_Chosen_Register), .WrData(Chosen_Write_Data), .WrReg(Stored_RegWrite),
    .RdAddr1(Source_Register), .RdAddr2(Target_Register), .RdData1(register_file_1_rddata1),
    .RdData2(register_file_1_rddata2), .Clock(Clock));
  // Probe on bit_extender_1_out
  assign bit_extender_1_out = {{16{1'b0}}, {Destination_Register, Shmt, Funct}};  // Bit_Extender bit_extender_1
  // Probe on Saved_Next_Instruction
  // Probe on register_file_1_rddata1
  // Probe on register_file_1_rddata2
  // Probe on Source_Register
  // Probe on Target_Register
  // Probe on Destination_Register
  // Probe on Funct
  WB wb_1 (
    .RegWrite(RegWrite), .MemtoReg(MemtoReg), .Clock(Clock), .Saved_RegWrite(Saved_RegWrite),
    .Saved_MemtoReg(Saved_MemtoReg));
  M m_1 (
    .MemRead(MemRead), .MemWrite(MemWrite), .Clock(Clock), .Saved_MemRead(Saved_MemRead),
    .Saved_MemWrite(Saved_MemWrite));
  EX ex_1 (
    .RegDst(RegDst), .ALUOp(ALUOp), .ALUSrc(ALUSrc), .Branch(Branch), .Clock(Clock),
    .Saved_RegDst(Saved_RegDst), .Saved_ALUOp(Saved_ALUOp), .Saved_ALUSrc(Saved_ALUSrc),
    .Saved_Branch(Saved_Branch));
  ID_EX id_ex_1 (
    .Saved_Next_Instruction(Saved_Next_Instruction), .Read_data_2(register_file_1_rddata2),
    .Read_data_1(register_file_1_rddata1), .Sign_Extended_Instruction(bit_extender_1_out),
    .Source_Register(Source_Register), .Destination_Register(Destination_Register), .Clock(Clock),
    .Passed_Next_Instruction(Passed_Next_Instruction), .Saved_Read_data_2(Saved_Read_data_2),
    .Saved_Read_data_1(Saved_Read_data_1), .Saved_Sign_Extended_Instruction(Saved_Sign_Extended_Instruction),
    .Saved_Source_Register(Saved_Source_Register), .Saved_Destination_Register(Saved_Destination_Register),
    .Funct(Funct), .Saved_Funct(Saved_Funct), .Shmt(Shmt), .Saved_Shmt(Saved_Shmt),
    .Saved_Target_Register(Saved_Target_Register), .Target_Register(Target_Register));
  // Probe on Passed_Next_Instruction
  // Probe on Saved_Read_data_1
  // Probe on Saved_Read_data_2
  // Probe on Saved_Sign_Extended_Instruction
  // Probe on Saved_Source_Register
  // Probe on Saved_Target_Register
  // Probe on Saved_Destination_Register
  // Probe on Saved_Funct
  // Probe on Saved_Source_Register
  // Probe on Saved_Target_Register
  // Probe on Passed_Chosen_Register
  // Probe on Saved_Chosen_Register
  // Probe on Saved_ALUOp
  // Probe on Saved_Funct
  // Probe on Chosen_Write_Data
  // Probe on Chosen_Write_Data
  // Probe on Saved_Read_data_2
  // Probe on Saved_ALU_Result
  ALU_Control alu_control_1 (.ALUOp(Saved_ALUOp), .Funct(Saved_Funct), .ALUCtl(ALUCtl));
  // Probe on Saved_Read_data_1
  // Probe on Saved_ALU_Result
  // Probe on ForwardB
  Multiplexer #(.select(2), .width(32), .enable("false")) multiplexer_2 (
    .in0(Saved_Read_data_2), .in1(Chosen_Write_Data), .in2(Saved_ALU_Result), .out(multiplexer_2_out),
    .sel(ForwardB));  // open: in3
  // Probe on ALUCtl
  // Probe on ForwardA
  Multiplexer #(.select(2), .width(32), .enable("false")) multiplexer_3 (
    .in0(Saved_Read_data_1), .in1(Chosen_Write_Data), .in2(Saved_ALU_Result), .out(multiplexer_3_out),
    .sel(ForwardA));  // open: in3
  Comparator #(.width(5)) comparator_1 (
    .a(Saved_Target_Register), .b(Saved_Chosen_Register), .eq(comparator_1_eq));  // open: gt, lt
  // Probe on multiplexer_2_out
  and and_1 (and_1_out, Saved_MemWrite, comparator_1_eq);
  // Probe on Saved_Sign_Extended_Instruction
  Multiplexer #(.width(32), .enable("false")) multiplexer_4 (
    .in0(Saved_Read_data_2), .in1(Saved_ALU_Result), .out(multiplexer_4_out), .sel(and_1_out));
  Forwarding_Unit forwarding_unit_1 (
    .ForwardA(ForwardA), .ForwardB(ForwardB), .ID_EX_Target_Register(Saved_Target_Register),
    .ID_EX_Source_Register(Saved_Source_Register), .MEM_WB_Destination_Register(Passed_Chosen_Register),
    .MEM_WB_RegWrite(Stored_RegWrite), .EX_MEM_RegWrite(Passed_RegWrite),
    .EX_MEM_Destination_Register(Saved_Chosen_Register));
  Multiplexer #(.width(32), .enable("false")) multiplexer_5 (
    .in0(multiplexer_2_out), .in1(Saved_Sign_Extended_Instruction), .out(multiplexer_5_out),
    .sel(Saved_ALUSrc));
  // Probe on multiplexer_5_out
  Shifter #(.width(32)) shifter_1 (.in(Saved_Sign_Extended_Instruction), .\dist (5'b00010), .out(shifter_1_out));
  // Probe on multiplexer_3_out
  // Probe on Saved_Target_Register
  // Probe on Saved_Destination_Register
  Adder #(.width(32)) adder_2 (.a(Passed_Next_Instruction), .b(shifter_1_out), .out(adder_2_out));  // open: cin, cout
  ALU alu_1 (
    .ALUCtl(ALUCtl), .A(multiplexer_3_out), .B(multiplexer_5_out), .ALUResult(alu_1_aluresult),
    .Zero(alu_1_zero), .Shamt(Saved_Shmt));  // open: Overflow
  Multiplexer #(.width(5), .enable("false")) multiplexer_6 (
    .in0(Saved_Target_Register), .in1(Saved_Destination_Register), .out(multiplexer_6_out), .sel(Saved_RegDst));
  // Probe on alu_1_aluresult
  // Probe on multiplexer_4_out
  // Probe on multiplexer_6_out
  EX ex_2 (
    .Branch(Saved_Branch), .Clock(Clock), .Saved_Branch(Passed_Branch));  // open: RegDst, ALUOp, ALUSrc, Saved_RegDst, Saved_ALUOp, Saved_ALUSrc
  WB wb_2 (
    .RegWrite(Saved_RegWrite), .MemtoReg(Saved_MemtoReg), .Clock(Clock), .Saved_RegWrite(Passed_RegWrite),
    .Saved_MemtoReg(Passed_MemtoReg));
  M m_2 (
    .MemRead(Saved_MemRead), .MemWrite(Saved_MemWrite), .Clock(Clock), .Saved_MemRead(Passed_MemRead),
    .Saved_MemWrite(Passed_MemWrite));
  EX_MEM ex_mem_1 (
    .Adder_Result(adder_2_out), .Zero(alu_1_zero), .ALU_Result(alu_1_aluresult),
    .Saved_Read_data_2(multiplexer_4_out), .Chosen_Register(multiplexer_6_out), .Clock(Clock),
    .Saved_Adder_Result(Saved_Adder_Result), .Saved_Zero_Value(Saved_Zero_Value),
    .Saved_ALU_Result(Saved_ALU_Result), .Passed_Read_data_2(Passed_Read_data_2),
    .Saved_Chosen_Register(Saved_Chosen_Register));
  // Probe on Saved_ALU_Result
  // Probe on Passed_Read_data_2
  // Probe on Saved_Chosen_Register
  and and_2 (PCSrc, Passed_Branch, Saved_Zero_Value);
  // Probe on Saved_ALU_Result[7:0]
  // Probe on Passed_Read_data_2
  // Probe on ram_1_data
  RAM #(.dataWidth(32), .bus("separate")) ram_1 (
    .addr(Saved_ALU_Result[7:0]), .din(Passed_Read_data_2), .data(ram_1_data), .str(Passed_MemWrite),
    .clk(Clock), .ld(Passed_MemRead));  // open: sel, clr
  // Probe on Saved_ALU_Result
  // Probe on Saved_Chosen_Register
  WB wb_3 (
    .RegWrite(Passed_RegWrite), .MemtoReg(Passed_MemtoReg), .Clock(Clock), .Saved_RegWrite(Stored_RegWrite),
    .Saved_MemtoReg(Stored_MemtoReg));
  // Probe on Saved_Mem_Data
  MEM_WB mem_wb_1 (
    .Mem_Data(ram_1_data), .Saved_ALU_Result(Saved_ALU_Result),
    .Saved_Chosen_Register(Saved_Chosen_Register), .Clock(Clock), .Saved_Mem_Data(Saved_Mem_Data),
    .Passed_ALU_Result(Passed_ALU_Result), .Passed_Chosen_Register(Passed_Chosen_Register));
  // Probe on Passed_ALU_Result
  // Probe on Passed_Chosen_Register
  // Probe on Passed_ALU_Result
  // Probe on nothing
  // Probe on nothing
  // Probe on nothing
  // Probe on nothing
  // Probe on nothing
  // Probe on nothing
  // Probe on nothing
  // Probe on nothing
  // Probe on nothing
  // Probe on nothing
  // Probe on Saved_Mem_Data
  Multiplexer #(.width(32), .enable("false")) multiplexer_7 (
    .in0(Passed_ALU_Result), .in1(Saved_Mem_Data), .out(Chosen_Write_Data), .sel(Stored_MemtoReg));
  // Probe on Chosen_Write_Data

  // Notes on the sheet:
  //   contents of rom_1 (hex, n*v repeats v):
  //   20010001 20020002 20030003 20040004 20050005 20060006 34270008 ac420012 434020 234824 455022 665825
  //   c76026 c7682a 17280 47842 30700002 eb8827 8d920005 2833000a 4aa02b
endmodule

module ALU (
  input  [3:0] ALUCtl,
  input  [31:0] A,
  input  [31:0] B,
  input  [4:0] Shamt,
  output [31:0] ALUResult,
  output Zero,
  output Overflow
);

  wire comparator_1_lt, comparator_2_lt, comparator_3_eq, comparator_4_eq, or_2_out;
  wire [31:0] ADD, AND, NOR, OR, SLL, SLT, SLTU, SRL, SUB, XOR;

  assign XOR = A ^ B;  // XOR_Gate xor_1, 32 bits wide
  Adder #(.width(32)) adder_1 (.a(A), .b(B), .out(ADD));  // open: cin, cout
  Subtractor #(.width(32)) subtractor_1 (.a(A), .b(B), .out(SUB));  // open: bin, bout
  assign AND = A & B;  // AND_Gate and_1, 32 bits wide
  assign OR = A | B;  // OR_Gate or_1, 32 bits wide
  assign NOR = ~(A | B);  // NOR_Gate nor_1, 32 bits wide
  Comparator #(.width(32)) comparator_1 (.a(A), .b(B), .lt(comparator_1_lt));  // open: gt, eq
  assign SLT = {{31{1'b0}}, comparator_1_lt};  // Bit_Extender bit_extender_1
  Shifter #(.width(32)) shifter_1 (.in(B), .\dist (Shamt), .out(SLL));
  Shifter #(.width(32), .shift("lr")) shifter_2 (.in(B), .\dist (Shamt), .out(SRL));
  Comparator #(.width(32), .mode("unsigned")) comparator_2 (.a(A), .b(B), .lt(comparator_2_lt));  // open: gt, eq
  assign SLTU = {{31{1'b0}}, comparator_2_lt};  // Bit_Extender bit_extender_2
  Multiplexer #(.select(4), .width(32), .enable("false")) multiplexer_1 (
    .in0(XOR), .in1(SLTU), .in2(SLT), .in3(AND), .in4(NOR), .in5(SUB), .in6(OR), .in7(ADD), .in8(SRL),
    .in9(SLL), .out(ALUResult), .sel(ALUCtl));  // open: in10, in11, in12, in13, in14, in15
  Comparator #(.width(4)) comparator_3 (.a(4'b0111), .b(ALUCtl), .eq(comparator_3_eq));  // open: gt, lt
  Comparator #(.width(4)) comparator_4 (.a(ALUCtl), .b(4'b0101), .eq(comparator_4_eq));  // open: gt, lt
  Overflow_Unit overflow_unit_1 (
    .Add(comparator_3_eq), .Sub(comparator_4_eq), .ASign(A[31]), .BSign(B[31]), .ResultSign(ALUResult[31]),
    .Overflow(Overflow));
  or or_2 (or_2_out, ALUResult[0], ALUResult[1], ALUResult[2], ALUResult[3], ALUResult[4], ALUResult[5], ALUResult[6], ALUResult[7], ALUResult[8], ALUResult[9], ALUResult[10], ALUResult[11], ALUResult[12], ALUResult[13], ALUResult[14], ALUResult[15], ALUResult[16], ALUResult[17], ALUResult[18], ALUResult[19], ALUResult[20], ALUResult[21], ALUResult[22], ALUResult[23], ALUResult[24], ALUResult[25], ALUResult[26], ALUResult[27], ALUResult[28], ALUResult[29], ALUResult[30], ALUResult[31]);
  not not_1 (Zero, or_2_out);

  // Other names for the same wires on the sheet: ASign = A[31]; ResultSign = ALUResult[31]; BSign = B[31]

  // Notes on the sheet:
  //   ALUCtl for ADD on top port
  //   ALUCtl for SUB on second port
endmodule

module Register_File (
  input  [4:0] WrAddr,
  input  [31:0] WrData,
  input  WrReg,
  input  [4:0] RdAddr1,
  input  [4:0] RdAddr2,
  input  Clock,
  output [31:0] RdData1,
  output [31:0] RdData2
);

  wire and_1_out, and_2_out, comparator_1_eq, comparator_2_eq, comparator_3_eq, comparator_4_eq, not_1_out,
       not_2_out, WrReg0, WrReg1, WrReg2, WrReg3, WrReg4, WrReg5, WrReg6, WrReg7, WrReg8, WrReg9, WrReg10,
       WrReg11, WrReg12, WrReg13, WrReg14, WrReg15, WrReg16, WrReg17, WrReg18, WrReg19, WrReg20, WrReg21,
       WrReg22, WrReg23, WrReg24, WrReg25, WrReg26, WrReg27, WrReg28, WrReg29, WrReg30, WrReg31;
  wire [31:0] multiplexer_1_out, multiplexer_2_out, RegData1, RegData2, RegData3, RegData4, RegData5,
       RegData6, RegData7, RegData8, RegData9, RegData10, RegData11, RegData12, RegData13, RegData14,
       RegData15, RegData16, RegData17, RegData18, RegData19, RegData20, RegData21, RegData22, RegData23,
       RegData24, RegData25, RegData26, RegData27, RegData28, RegData29, RegData30, RegData31;

  Demultiplexer #(.select(5), .enable("false")) demultiplexer_1 (
    .out0(WrReg0), .out1(WrReg1), .out2(WrReg2), .out3(WrReg3), .out4(WrReg4), .out5(WrReg5), .out6(WrReg6),
    .out7(WrReg7), .out8(WrReg8), .out9(WrReg9), .out10(WrReg10), .out11(WrReg11), .out12(WrReg12),
    .out13(WrReg13), .out14(WrReg14), .out15(WrReg15), .out16(WrReg16), .out17(WrReg17), .out18(WrReg18),
    .out19(WrReg19), .out20(WrReg20), .out21(WrReg21), .out22(WrReg22), .out23(WrReg23), .out24(WrReg24),
    .out25(WrReg25), .out26(WrReg26), .out27(WrReg27), .out28(WrReg28), .out29(WrReg29), .out30(WrReg30),
    .out31(WrReg31), .in(WrReg), .sel(WrAddr));
  // Probe on RegData4
  Register #(.width(32)) Reg4 (.D(WrData), .en(WrReg4), .Q(RegData4), .clk(Clock));  // open: clr
  // Probe on RegData8
  Register #(.width(32)) Reg8 (.D(WrData), .en(WrReg8), .Q(RegData8), .clk(Clock));  // open: clr
  // Probe on RegData12
  Register #(.width(32)) Reg12 (.D(WrData), .en(WrReg12), .Q(RegData12), .clk(Clock));  // open: clr
  // Probe on RegData16
  Register #(.width(32)) Reg16 (.D(WrData), .en(WrReg16), .Q(RegData16), .clk(Clock));  // open: clr
  // Probe on RegData20
  Register #(.width(32)) Reg20 (.D(WrData), .en(WrReg20), .Q(RegData20), .clk(Clock));  // open: clr
  // Probe on RegData24
  Register #(.width(32)) Reg24 (.D(WrData), .en(WrReg24), .Q(RegData24), .clk(Clock));  // open: clr
  // Probe on RegData28
  Register #(.width(32)) Reg28 (.D(WrData), .en(WrReg28), .Q(RegData28), .clk(Clock));  // open: clr
  Register #(.width(32)) Reg1 (.D(WrData), .en(WrReg1), .Q(RegData1), .clk(Clock));  // open: clr
  Register #(.width(32)) Reg5 (.D(WrData), .en(WrReg5), .Q(RegData5), .clk(Clock));  // open: clr
  Register #(.width(32)) Reg9 (.D(WrData), .en(WrReg9), .Q(RegData9), .clk(Clock));  // open: clr
  Register #(.width(32)) Reg13 (.D(WrData), .en(WrReg13), .Q(RegData13), .clk(Clock));  // open: clr
  Register #(.width(32)) Reg17 (.D(WrData), .en(WrReg17), .Q(RegData17), .clk(Clock));  // open: clr
  Register #(.width(32)) Reg21 (.D(WrData), .en(WrReg21), .Q(RegData21), .clk(Clock));  // open: clr
  Register #(.width(32)) Reg25 (.D(WrData), .en(WrReg25), .Q(RegData25), .clk(Clock));  // open: clr
  Register #(.width(32)) Reg29 (.D(WrData), .en(WrReg29), .Q(RegData29), .clk(Clock));  // open: clr
  // Probe on RegData1
  // Probe on RegData5
  // Probe on RegData9
  // Probe on RegData13
  // Probe on RegData17
  // Probe on RegData21
  // Probe on RegData25
  // Probe on RegData29
  // Probe on RegData2
  Register #(.width(32)) Reg2 (.D(WrData), .en(WrReg2), .Q(RegData2), .clk(Clock));  // open: clr
  // Probe on RegData6
  Register #(.width(32)) Reg6 (.D(WrData), .en(WrReg6), .Q(RegData6), .clk(Clock));  // open: clr
  // Probe on RegData10
  Register #(.width(32)) Reg10 (.D(WrData), .en(WrReg10), .Q(RegData10), .clk(Clock));  // open: clr
  // Probe on RegData14
  Register #(.width(32)) Reg14 (.D(WrData), .en(WrReg14), .Q(RegData14), .clk(Clock));  // open: clr
  // Probe on RegData18
  Register #(.width(32)) Reg18 (.D(WrData), .en(WrReg18), .Q(RegData18), .clk(Clock));  // open: clr
  // Probe on RegData22
  Register #(.width(32)) Reg22 (.D(WrData), .en(WrReg22), .Q(RegData22), .clk(Clock));  // open: clr
  // Probe on RegData26
  Register #(.width(32)) Reg26 (.D(WrData), .en(WrReg26), .Q(RegData26), .clk(Clock));  // open: clr
  // Probe on RegData30
  Register #(.width(32)) Reg30 (.D(WrData), .en(WrReg30), .Q(RegData30), .clk(Clock));  // open: clr
  // Probe on RegData3
  Register #(.width(32)) Reg3 (.D(WrData), .en(WrReg3), .Q(RegData3), .clk(Clock));  // open: clr
  // Probe on RegData7
  Register #(.width(32)) Reg7 (.D(WrData), .en(WrReg7), .Q(RegData7), .clk(Clock));  // open: clr
  // Probe on RegData11
  Register #(.width(32)) Reg11 (.D(WrData), .en(WrReg11), .Q(RegData11), .clk(Clock));  // open: clr
  // Probe on RegData15
  Register #(.width(32)) Reg15 (.D(WrData), .en(WrReg15), .Q(RegData15), .clk(Clock));  // open: clr
  // Probe on RegData19
  Register #(.width(32)) Reg19 (.D(WrData), .en(WrReg19), .Q(RegData19), .clk(Clock));  // open: clr
  // Probe on RegData23
  Register #(.width(32)) Reg23 (.D(WrData), .en(WrReg23), .Q(RegData23), .clk(Clock));  // open: clr
  // Probe on RegData27
  Register #(.width(32)) Reg27 (.D(WrData), .en(WrReg27), .Q(RegData27), .clk(Clock));  // open: clr
  // Probe on RegData31
  Register #(.width(32)) Reg31 (.D(WrData), .en(WrReg31), .Q(RegData31), .clk(Clock));  // open: clr
  Multiplexer #(.select(5), .width(32), .enable("false")) multiplexer_1 (
    .in0({32{1'b0}}), .in1(RegData1), .in2(RegData2), .in3(RegData3), .in4(RegData4), .in5(RegData5),
    .in6(RegData6), .in7(RegData7), .in8(RegData8), .in9(RegData9), .in10(RegData10), .in11(RegData11),
    .in12(RegData12), .in13(RegData13), .in14(RegData14), .in15(RegData15), .in16(RegData16),
    .in17(RegData17), .in18(RegData18), .in19(RegData19), .in20(RegData20), .in21(RegData21),
    .in22(RegData22), .in23(RegData23), .in24(RegData24), .in25(RegData25), .in26(RegData26),
    .in27(RegData27), .in28(RegData28), .in29(RegData29), .in30(RegData30), .in31(RegData31),
    .out(multiplexer_1_out), .sel(RdAddr1));
  Multiplexer #(.select(5), .width(32), .enable("false")) multiplexer_2 (
    .in0({32{1'b0}}), .in1(RegData1), .in2(RegData2), .in3(RegData3), .in4(RegData4), .in5(RegData5),
    .in6(RegData6), .in7(RegData7), .in8(RegData8), .in9(RegData9), .in10(RegData10), .in11(RegData11),
    .in12(RegData12), .in13(RegData13), .in14(RegData14), .in15(RegData15), .in16(RegData16),
    .in17(RegData17), .in18(RegData18), .in19(RegData19), .in20(RegData20), .in21(RegData21),
    .in22(RegData22), .in23(RegData23), .in24(RegData24), .in25(RegData25), .in26(RegData26),
    .in27(RegData27), .in28(RegData28), .in29(RegData29), .in30(RegData30), .in31(RegData31),
    .out(multiplexer_2_out), .sel(RdAddr2));
  Multiplexer #(.width(32), .enable("false")) multiplexer_3 (
    .in0(multiplexer_1_out), .in1(WrData), .out(RdData1), .sel(and_1_out));
  Comparator #(.width(5), .mode("unsigned")) comparator_1 (
    .a(WrAddr), .b(RdAddr2), .eq(comparator_1_eq));  // open: gt, lt
  Multiplexer #(.width(32), .enable("false")) multiplexer_4 (
    .in0(multiplexer_2_out), .in1(WrData), .out(RdData2), .sel(and_2_out));
  Comparator #(.width(5), .mode("unsigned")) comparator_2 (
    .a(WrAddr), .b(RdAddr1), .eq(comparator_2_eq));  // open: gt, lt
  and and_1 (and_1_out, comparator_2_eq, WrReg, not_1_out);
  and and_2 (and_2_out, comparator_1_eq, WrReg, not_2_out);
  Comparator #(.width(5), .mode("unsigned")) comparator_3 (
    .a(WrAddr), .b({5{1'b0}}), .eq(comparator_3_eq));  // open: gt, lt
  not not_1 (not_1_out, comparator_3_eq);
  Comparator #(.width(5), .mode("unsigned")) comparator_4 (
    .a(WrAddr), .b({5{1'b0}}), .eq(comparator_4_eq));  // open: gt, lt
  not not_2 (not_2_out, comparator_4_eq);
endmodule

module Overflow_Unit (
  input  Add,
  input  Sub,
  input  ASign,
  input  BSign,
  input  ResultSign,
  output Overflow
);

  wire and_1_out, and_2_out, or_1_out, xnor_1_out, xor_1_out, xor_2_out;

  xnor xnor_1 (xnor_1_out, ASign, BSign);
  xor xor_1 (xor_1_out, ASign, BSign);
  and and_1 (and_1_out, xnor_1_out, Add);
  and and_2 (and_2_out, xor_1_out, Sub);
  or or_1 (or_1_out, and_1_out, and_2_out);
  xor xor_2 (xor_2_out, ResultSign, ASign);
  and and_3 (Overflow, or_1_out, xor_2_out);

  // Notes on the sheet:
  //   Overflow occurs when doing addition and sign(A) == sign(B) && sign(result) != sign(A)
  //   Or
  //   Overflow occurs when doing subtraction and sign(A) != sign(B) && sign(result) != sign(A)
endmodule

module WB (
  input  RegWrite,
  input  MemtoReg,
  input  Clock,
  output Saved_RegWrite,
  output Saved_MemtoReg
);

  Register #(.width(1)) u_RegWrite (.D(RegWrite), .Q(Saved_RegWrite), .clk(Clock));  // open: en, clr
  Register #(.width(1)) u_MemtoReg (.D(MemtoReg), .Q(Saved_MemtoReg), .clk(Clock));  // open: en, clr
endmodule

module M (
  input  MemRead,
  input  MemWrite,
  input  Clock,
  output Saved_MemRead,
  output Saved_MemWrite
);

  Register #(.width(1)) u_MemRead (.D(MemRead), .Q(Saved_MemRead), .clk(Clock));  // open: en, clr
  Register #(.width(1)) u_MemWrite (.D(MemWrite), .Q(Saved_MemWrite), .clk(Clock));  // open: en, clr
endmodule

module EX (
  input  RegDst,
  input  [1:0] ALUOp,
  input  ALUSrc,
  input  Branch,
  input  Clock,
  output Saved_RegDst,
  output [1:0] Saved_ALUOp,
  output Saved_ALUSrc,
  output Saved_Branch
);

  Register #(.width(1)) u_RegDst (.D(RegDst), .Q(Saved_RegDst), .clk(Clock));  // open: en, clr
  Register #(.width(2)) u_ALUOp (.D(ALUOp), .Q(Saved_ALUOp), .clk(Clock));  // open: en, clr
  Register #(.width(1)) u_ALUSrc (.D(ALUSrc), .Q(Saved_ALUSrc), .clk(Clock));  // open: en, clr
  Register #(.width(1)) u_Branch (.D(Branch), .Q(Saved_Branch), .clk(Clock));  // open: en, clr
endmodule

module IF_ID (
  input  [31:0] Next_Instruction,
  input  [31:0] Current_Instruction,
  input  Clock,
  output [31:0] Saved_Next_Instruction,
  output [31:0] Current_Instruction_2
);

  Register #(.width(32)) u_Next_Instruction (
    .D(Next_Instruction), .Q(Saved_Next_Instruction), .clk(Clock));  // open: en, clr
  Register #(.width(32)) u_Current_Instruction (
    .D(Current_Instruction), .Q(Current_Instruction_2), .clk(Clock));  // open: en, clr

  // Other names for the same wires on the sheet: Current_Instruction_t[31:0] = Current_Instruction_2;
  //   Instruction[31:0] = Current_Instruction
endmodule

module Main_Control (
  input  [5:0] Opcode,
  input  [5:0] Funct,
  output Branch,
  output ALUSrc,
  output [1:0] ALUOp,
  output RegDst,
  output MemWrite,
  output MemRead,
  output MemtoReg,
  output RegWrite
);

  ROM #(.addrWidth(12), .dataWidth(9)) rom_1 (
    .addr({Opcode, Funct}), .data({RegWrite, MemtoReg, MemRead, MemWrite, RegDst, ALUOp, ALUSrc, Branch}));  // open: sel

  // Notes on the sheet:
  //   contents of rom_1 (hex, n*v repeats v):
  //   118 0 118 29*0 118 0 118 0 4*118 0 0 118 118 212*0 64*5 192*0 64*102 64*0 64*10e 64*0 64*106 64*10a
  //   1344*0 64*1c2 448*0 64*22
endmodule

module ALU_Control (
  input  [1:0] ALUOp,
  input  [5:0] Funct,
  output [3:0] ALUCtl
);

  wire and_2_out, and_3_out, and_4_out, and_5_out, and_6_out, and_7_out, and_8_out, and_9_out, and_10_out,
       and_11_out, and_12_out, and_13_out, and_14_out, and_15_out, and_16_out, and_17_out, and_18_out,
       and_19_out, and_20_out, not_1_out, not_2_out, not_3_out, not_4_out, not_5_out, not_6_out, not_7_out,
       not_8_out, not_9_out, not_10_out, not_11_out, not_12_out, not_13_out, not_14_out, not_15_out,
       not_16_out, not_17_out, not_18_out, not_19_out, not_20_out, not_21_out, not_22_out, not_23_out,
       not_24_out, not_25_out, not_26_out, not_27_out, not_28_out, not_29_out, not_30_out, not_31_out,
       not_32_out, not_33_out, not_34_out, not_35_out, not_36_out, not_37_out, not_38_out, not_39_out,
       not_40_out, not_41_out, not_42_out, not_43_out, not_44_out, not_45_out, not_46_out;

  not not_1 (not_1_out, Funct[5]);
  not not_2 (not_2_out, Funct[4]);
  not not_3 (not_3_out, Funct[3]);
  not not_4 (not_4_out, Funct[2]);
  not not_5 (not_5_out, Funct[0]);
  not not_6 (not_6_out, ALUOp[1]);
  not not_7 (not_7_out, ALUOp[0]);
  not not_8 (not_8_out, ALUOp[0]);
  not not_9 (not_9_out, Funct[3]);
  not not_10 (not_10_out, ALUOp[0]);
  not not_11 (not_11_out, Funct[5]);
  not not_12 (not_12_out, ALUOp[0]);
  not not_13 (not_13_out, Funct[5]);
  not not_14 (not_14_out, ALUOp[0]);
  not not_15 (not_15_out, Funct[1]);
  not not_16 (not_16_out, ALUOp[0]);
  not not_17 (not_17_out, ALUOp[0]);
  not not_18 (not_18_out, Funct[4]);
  not not_19 (not_19_out, Funct[3]);
  not not_20 (not_20_out, Funct[2]);
  not not_21 (not_21_out, Funct[0]);
  not not_22 (not_22_out, Funct[4]);
  not not_23 (not_23_out, Funct[3]);
  not not_24 (not_24_out, Funct[3]);
  not not_25 (not_25_out, Funct[2]);
  not not_26 (not_26_out, Funct[5]);
  not not_27 (not_27_out, Funct[5]);
  not not_28 (not_28_out, Funct[0]);
  not not_29 (not_29_out, Funct[1]);
  not not_30 (not_30_out, Funct[4]);
  not not_31 (not_31_out, Funct[3]);
  not not_32 (not_32_out, Funct[2]);
  not not_33 (not_33_out, Funct[1]);
  not not_34 (not_34_out, Funct[0]);
  not not_35 (not_35_out, Funct[4]);
  not not_36 (not_36_out, Funct[3]);
  not not_37 (not_37_out, Funct[2]);
  not not_38 (not_38_out, Funct[0]);
  not not_39 (not_39_out, Funct[4]);
  not not_40 (not_40_out, Funct[3]);
  not not_41 (not_41_out, Funct[1]);
  not not_42 (not_42_out, Funct[0]);
  not not_43 (not_43_out, Funct[4]);
  not not_44 (not_44_out, Funct[2]);
  and and_1 (ALUCtl[3], ALUOp[1], not_1_out, not_2_out, not_3_out, not_4_out, not_5_out);
  and and_2 (and_2_out, not_6_out, not_7_out);
  and and_3 (and_3_out, not_8_out, not_9_out, Funct[0]);
  and and_4 (and_4_out, not_10_out, not_11_out, Funct[2]);
  and and_5 (and_5_out, not_12_out, not_13_out, Funct[3]);
  and and_6 (and_6_out, not_14_out, Funct[3], not_15_out);
  and and_7 (and_7_out, not_16_out, Funct[3], Funct[2]);
  and and_8 (and_8_out, not_17_out, Funct[4]);
  and and_9 (and_9_out, ALUOp[1], Funct[5], not_18_out, not_19_out, not_20_out, not_21_out);
  and and_10 (and_10_out, ALUOp[1], Funct[5], not_22_out, not_23_out, Funct[2], Funct[0]);
  not not_45 (not_45_out, ALUOp[1]);
  and and_11 (and_11_out, not_24_out, not_25_out, Funct[0]);
  and and_12 (and_12_out, not_26_out, Funct[2]);
  and and_13 (and_13_out, not_27_out, Funct[3]);
  and and_14 (and_14_out, Funct[3], not_28_out);
  and and_15 (and_15_out, Funct[3], Funct[2]);
  and and_16 (and_16_out, Funct[5], not_29_out);
  not not_46 (not_46_out, ALUOp[1]);
  and and_17 (and_17_out, not_30_out, not_31_out, not_32_out, not_33_out, not_34_out);
  and and_18 (and_18_out, Funct[5], not_35_out, not_36_out, not_37_out, not_38_out);
  and and_19 (and_19_out, Funct[5], not_39_out, not_40_out, not_41_out, not_42_out);
  and and_20 (and_20_out, Funct[5], not_43_out, Funct[3], not_44_out, Funct[1], Funct[0]);
  or or_1 (ALUCtl[2], and_2_out, and_3_out, and_4_out, and_5_out, and_6_out, and_7_out, and_8_out, and_9_out, and_10_out);
  or or_2 (ALUCtl[1], not_45_out, and_11_out, and_12_out, and_13_out, and_14_out, and_15_out, Funct[4], and_16_out);
  or or_3 (ALUCtl[0], not_46_out, and_17_out, and_18_out, and_19_out, and_20_out);

  // Other names for the same wires on the sheet: F0 = Funct[0]; F1 = Funct[1]; F2 = Funct[2]; F3 = Funct[3];
  //   F4 = Funct[4]; F5 = Funct[5]
endmodule

module ID_EX (
  input  [31:0] Saved_Next_Instruction,
  input  [31:0] Read_data_1,
  input  [31:0] Read_data_2,
  input  [31:0] Sign_Extended_Instruction,
  input  [4:0] Source_Register,
  input  [4:0] Target_Register,
  input  [4:0] Destination_Register,
  input  [5:0] Funct,
  input  [4:0] Shmt,
  input  Clock,
  output [31:0] Passed_Next_Instruction,
  output [31:0] Saved_Read_data_1,
  output [31:0] Saved_Read_data_2,
  output [31:0] Saved_Sign_Extended_Instruction,
  output [4:0] Saved_Source_Register,
  output [4:0] Saved_Target_Register,
  output [4:0] Saved_Destination_Register,
  output [5:0] Saved_Funct,
  output [4:0] Saved_Shmt
);

  Register #(.width(32)) u_Saved_Next_Instruction (
    .D(Saved_Next_Instruction), .Q(Passed_Next_Instruction), .clk(Clock));  // open: en, clr
  Register #(.width(32)) u_Saved_Read_data_1 (.D(Read_data_1), .Q(Saved_Read_data_1), .clk(Clock));  // open: en, clr
  Register #(.width(32)) u_Read_data_2 (.D(Read_data_2), .Q(Saved_Read_data_2), .clk(Clock));  // open: en, clr
  Register #(.width(32)) u_Sign_Extended_Instruction (
    .D(Sign_Extended_Instruction), .Q(Saved_Sign_Extended_Instruction), .clk(Clock));  // open: en, clr
  Register #(.width(5)) u_Source_Register (
    .D(Source_Register), .Q(Saved_Source_Register), .clk(Clock));  // open: en, clr
  Register #(.width(5)) u_Target_Register (
    .D(Target_Register), .Q(Saved_Target_Register), .clk(Clock));  // open: en, clr
  Register #(.width(5)) u_Destination_Register (
    .D(Destination_Register), .Q(Saved_Destination_Register), .clk(Clock));  // open: en, clr
  Register #(.width(6)) u_Funct (.D(Funct), .Q(Saved_Funct), .clk(Clock));  // open: en, clr
  Register #(.width(5)) u_Shmt (.D(Shmt), .Q(Saved_Shmt), .clk(Clock));  // open: en, clr
endmodule

module EX_MEM (
  input  [31:0] Adder_Result,
  input  Zero,
  input  [31:0] ALU_Result,
  input  [31:0] Saved_Read_data_2,
  input  [4:0] Chosen_Register,
  input  Clock,
  output [31:0] Saved_Adder_Result,
  output Saved_Zero_Value,
  output [31:0] Saved_ALU_Result,
  output [31:0] Passed_Read_data_2,
  output [4:0] Saved_Chosen_Register
);

  wire Saved_Zero_Value_t;

  Register #(.width(32)) u_Adder_Result (.D(Adder_Result), .Q(Saved_Adder_Result), .clk(Clock));  // open: en, clr
  Register #(.width(1)) u_Zero (.D(Zero), .Q(Saved_Zero_Value_t), .clk(Clock));  // open: en, clr
  Register #(.width(32)) u_ALU_Result (.D(ALU_Result), .Q(Saved_ALU_Result), .clk(Clock));  // open: en, clr
  Register #(.width(32)) u_Saved_Read_data_2 (
    .D(Saved_Read_data_2), .Q(Passed_Read_data_2), .clk(Clock));  // open: en, clr
  Register #(.width(5)) u_Chosen_Register (
    .D(Chosen_Register), .Q(Saved_Chosen_Register), .clk(Clock));  // open: en, clr

  assign Saved_Zero_Value = Zero;
endmodule

module MEM_WB (
  input  [31:0] Mem_Data,
  input  [31:0] Saved_ALU_Result,
  input  [4:0] Saved_Chosen_Register,
  input  Clock,
  output [31:0] Saved_Mem_Data,
  output [31:0] Passed_ALU_Result,
  output [4:0] Passed_Chosen_Register
);

  Register #(.width(32)) u_Mem_Data (.D(Mem_Data), .Q(Saved_Mem_Data), .clk(Clock));  // open: en, clr
  Register #(.width(32)) u_Saved_ALU_Result (
    .D(Saved_ALU_Result), .Q(Passed_ALU_Result), .clk(Clock));  // open: en, clr
  Register #(.width(5)) Saved_ALU_Result_2 (
    .D(Saved_Chosen_Register), .Q(Passed_Chosen_Register), .clk(Clock));  // open: en, clr
endmodule

module Forwarding_Unit (
  input  [4:0] ID_EX_Source_Register,
  input  [4:0] ID_EX_Target_Register,
  input  [4:0] MEM_WB_Destination_Register,
  input  [4:0] EX_MEM_Destination_Register,
  input  MEM_WB_RegWrite,
  input  EX_MEM_RegWrite,
  output [1:0] ForwardA,
  output [1:0] ForwardB
);

  wire and_1_out, and_2_out, and_3_out, and_4_out, EX_MEM_Destination_Register____0,
       EX_MEM_Destination_Register____ID_EX_Source_Register,
       EX_MEM_Destination_Register____ID_EX_Target_Register,
       EX_MEM_Destination_Register___ID_EX_Source_Register,
       EX_MEM_Destination_Register___ID_EX_Target_Register, MEM_WB_Destination_Register____0,
       MEM_WB_Destination_Register___ID_EX_Source_Register,
       MEM_WB_Destination_Register___ID_EX_Target_Register, nand_1_out, nand_2_out, xor_1_out, xor_2_out,
       xor_3_out, xor_4_out, xor_5_out, xor_6_out, xor_7_out, xor_8_out, xor_9_out, xor_10_out, xor_11_out,
       xor_12_out, xor_13_out, xor_14_out, xor_15_out, xor_16_out, xor_17_out, xor_18_out, xor_19_out,
       xor_20_out, xor_21_out, xor_22_out, xor_23_out, xor_24_out, xor_25_out, xor_26_out, xor_27_out,
       xor_28_out, xor_29_out, xor_30_out, xor_31_out, xor_32_out, xor_33_out, xor_34_out, xor_35_out,
       xor_36_out, xor_37_out, xor_38_out, xor_39_out, xor_40_out;
  wire [1:0] multiplexer_1_out, multiplexer_2_out;

  xor xor_1 (xor_1_out, EX_MEM_Destination_Register[4], 1'b0);
  xor xor_2 (xor_2_out, EX_MEM_Destination_Register[3], 1'b0);
  xor xor_3 (xor_3_out, EX_MEM_Destination_Register[2], 1'b0);
  xor xor_4 (xor_4_out, EX_MEM_Destination_Register[1], 1'b0);
  xor xor_5 (xor_5_out, EX_MEM_Destination_Register[0], 1'b0);
  xor xor_6 (xor_6_out, EX_MEM_Destination_Register[4], ID_EX_Source_Register[4]);
  xor xor_7 (xor_7_out, EX_MEM_Destination_Register[3], ID_EX_Source_Register[3]);
  xor xor_8 (xor_8_out, EX_MEM_Destination_Register[2], ID_EX_Source_Register[2]);
  xor xor_9 (xor_9_out, EX_MEM_Destination_Register[1], ID_EX_Source_Register[1]);
  xor xor_10 (xor_10_out, EX_MEM_Destination_Register[0], ID_EX_Source_Register[0]);
  xor xor_11 (xor_11_out, EX_MEM_Destination_Register[4], ID_EX_Target_Register[4]);
  xor xor_12 (xor_12_out, EX_MEM_Destination_Register[3], ID_EX_Target_Register[3]);
  xor xor_13 (xor_13_out, EX_MEM_Destination_Register[2], ID_EX_Target_Register[2]);
  xor xor_14 (xor_14_out, EX_MEM_Destination_Register[1], ID_EX_Target_Register[1]);
  xor xor_15 (xor_15_out, EX_MEM_Destination_Register[0], ID_EX_Target_Register[0]);
  xor xor_16 (xor_16_out, MEM_WB_Destination_Register[4], 1'b0);
  xor xor_17 (xor_17_out, MEM_WB_Destination_Register[3], 1'b0);
  xor xor_18 (xor_18_out, MEM_WB_Destination_Register[2], 1'b0);
  xor xor_19 (xor_19_out, MEM_WB_Destination_Register[1], 1'b0);
  xor xor_20 (xor_20_out, MEM_WB_Destination_Register[0], 1'b0);
  or or_1 (EX_MEM_Destination_Register____0, xor_1_out, xor_2_out, xor_3_out, xor_4_out, xor_5_out);
  nor nor_1 (EX_MEM_Destination_Register___ID_EX_Source_Register, xor_6_out, xor_7_out, xor_8_out, xor_9_out, xor_10_out);
  nor nor_2 (EX_MEM_Destination_Register___ID_EX_Target_Register, xor_11_out, xor_12_out, xor_13_out, xor_14_out, xor_15_out);
  or or_2 (MEM_WB_Destination_Register____0, xor_16_out, xor_17_out, xor_18_out, xor_19_out, xor_20_out);
  xor xor_21 (xor_21_out, EX_MEM_Destination_Register[4], ID_EX_Source_Register[4]);
  xor xor_22 (xor_22_out, EX_MEM_Destination_Register[3], ID_EX_Source_Register[3]);
  xor xor_23 (xor_23_out, EX_MEM_Destination_Register[2], ID_EX_Source_Register[2]);
  xor xor_24 (xor_24_out, EX_MEM_Destination_Register[1], ID_EX_Source_Register[1]);
  xor xor_25 (xor_25_out, EX_MEM_Destination_Register[0], ID_EX_Source_Register[0]);
  xor xor_26 (xor_26_out, EX_MEM_Destination_Register[4], ID_EX_Target_Register[4]);
  xor xor_27 (xor_27_out, EX_MEM_Destination_Register[3], ID_EX_Target_Register[3]);
  xor xor_28 (xor_28_out, EX_MEM_Destination_Register[2], ID_EX_Target_Register[2]);
  xor xor_29 (xor_29_out, EX_MEM_Destination_Register[1], ID_EX_Target_Register[1]);
  xor xor_30 (xor_30_out, EX_MEM_Destination_Register[0], ID_EX_Target_Register[0]);
  xor xor_31 (xor_31_out, MEM_WB_Destination_Register[4], ID_EX_Source_Register[4]);
  xor xor_32 (xor_32_out, MEM_WB_Destination_Register[3], ID_EX_Source_Register[3]);
  xor xor_33 (xor_33_out, MEM_WB_Destination_Register[2], ID_EX_Source_Register[2]);
  xor xor_34 (xor_34_out, MEM_WB_Destination_Register[1], ID_EX_Source_Register[1]);
  xor xor_35 (xor_35_out, MEM_WB_Destination_Register[0], ID_EX_Source_Register[0]);
  xor xor_36 (xor_36_out, MEM_WB_Destination_Register[4], ID_EX_Target_Register[4]);
  xor xor_37 (xor_37_out, MEM_WB_Destination_Register[3], ID_EX_Target_Register[3]);
  xor xor_38 (xor_38_out, MEM_WB_Destination_Register[2], ID_EX_Target_Register[2]);
  xor xor_39 (xor_39_out, MEM_WB_Destination_Register[1], ID_EX_Target_Register[1]);
  xor xor_40 (xor_40_out, MEM_WB_Destination_Register[0], ID_EX_Target_Register[0]);
  or or_3 (EX_MEM_Destination_Register____ID_EX_Source_Register, xor_21_out, xor_22_out, xor_23_out, xor_24_out, xor_25_out);
  or or_4 (EX_MEM_Destination_Register____ID_EX_Target_Register, xor_26_out, xor_27_out, xor_28_out, xor_29_out, xor_30_out);
  nor nor_3 (MEM_WB_Destination_Register___ID_EX_Source_Register, xor_31_out, xor_32_out, xor_33_out, xor_34_out, xor_35_out);
  nor nor_4 (MEM_WB_Destination_Register___ID_EX_Target_Register, xor_36_out, xor_37_out, xor_38_out, xor_39_out, xor_40_out);
  nand nand_1 (nand_1_out, EX_MEM_RegWrite, EX_MEM_Destination_Register____0, EX_MEM_Destination_Register____ID_EX_Target_Register);
  nand nand_2 (nand_2_out, EX_MEM_RegWrite, EX_MEM_Destination_Register____0, EX_MEM_Destination_Register____ID_EX_Source_Register);
  and and_1 (and_1_out, MEM_WB_RegWrite, MEM_WB_Destination_Register____0, MEM_WB_Destination_Register___ID_EX_Source_Register, nand_2_out);
  and and_2 (and_2_out, MEM_WB_RegWrite, MEM_WB_Destination_Register____0, MEM_WB_Destination_Register___ID_EX_Target_Register, nand_1_out);
  and and_3 (and_3_out, EX_MEM_RegWrite, EX_MEM_Destination_Register____0, EX_MEM_Destination_Register___ID_EX_Source_Register);
  Multiplexer #(.width(2), .enable("false")) multiplexer_1 (
    .in0(2'b00), .in1(2'b01), .out(multiplexer_1_out), .sel(and_1_out));
  Multiplexer #(.width(2), .enable("false")) multiplexer_2 (
    .in0(2'b00), .in1(2'b01), .out(multiplexer_2_out), .sel(and_2_out));
  Multiplexer #(.width(2), .enable("false")) multiplexer_3 (
    .in0(multiplexer_1_out), .in1(2'b10), .out(ForwardA), .sel(and_3_out));
  and and_4 (and_4_out, EX_MEM_RegWrite, EX_MEM_Destination_Register____0, EX_MEM_Destination_Register___ID_EX_Target_Register);
  Multiplexer #(.width(2), .enable("false")) multiplexer_4 (
    .in0(multiplexer_2_out), .in1(2'b10), .out(ForwardB), .sel(and_4_out));

  // Other names for the same wires on the sheet: EX_MEM_Destination_Register_0 = EX_MEM_Destination_Register[0];
  //   EX_MEM_Destination_Register_1 = EX_MEM_Destination_Register[1];
  //   EX_MEM_Destination_Register_2 = EX_MEM_Destination_Register[2];
  //   EX_MEM_Destination_Register_3 = EX_MEM_Destination_Register[3];
  //   EX_MEM_Destination_Register_4 = EX_MEM_Destination_Register[4];
  //   ID_EX_Source_Register_0 = ID_EX_Source_Register[0]; ID_EX_Source_Register_1 = ID_EX_Source_Register[1];
  //   ID_EX_Source_Register_2 = ID_EX_Source_Register[2]; ID_EX_Source_Register_3 = ID_EX_Source_Register[3];
  //   ID_EX_Source_Register_4 = ID_EX_Source_Register[4]; ID_EX_Target_Register_0 = ID_EX_Target_Register[0];
  //   ID_EX_Target_Register_1 = ID_EX_Target_Register[1]; ID_EX_Target_Register_2 = ID_EX_Target_Register[2];
  //   ID_EX_Target_Register_3 = ID_EX_Target_Register[3]; ID_EX_Target_Register_4 = ID_EX_Target_Register[4];
  //   MEM_WB_Destination_Register_0 = MEM_WB_Destination_Register[0];
  //   MEM_WB_Destination_Register_1 = MEM_WB_Destination_Register[1];
  //   MEM_WB_Destination_Register_2 = MEM_WB_Destination_Register[2];
  //   MEM_WB_Destination_Register_3 = MEM_WB_Destination_Register[3];
  //   MEM_WB_Destination_Register_4 = MEM_WB_Destination_Register[4]
endmodule
